// Logisim project epsCircuito.circ as structural Verilog: 4 circuits, main circuit main
module main (
  input  reset
);

  wire A_out, alguien_espera, and_6_out, and_7_out, and_8_out, C1_out, C2_out, C3_out, ck, desocupado, hayA,
       hayN, hayP, llamar_ya, llenaA, llenaN, llenaP, N_out, ni_P_ni_A, no_hayA, no_hayP, no_llenaA,
       no_llenaN, no_llenaP, nuevoA, nuevoN, nuevoP, P_out, pC1, pC2, pC3, register_2_q, register_3_q,
       register_4_q, sigA, sigN, sigP;
  wire [3:0] a_decimal_1_decenas, a_decimal_1_unidades, a_decimal_2_decenas, a_decimal_2_unidades,
       a_decimal_3_decenas, a_decimal_3_unidades, a_decimal_4_decenas, a_decimal_4_unidades, atendidosA,
       atendidosN, atendidosP, cub_1o2, cub_sig, dadosA, dadosN, dadosP, register_1_q, register_5_q,
       register_6_q, register_7_q, register_8_q, S_AoN, S_sig;

  Clock reloj (.out(ck));
  Button N (.out(N_out));
  Button A (.out(A_out));
  Button P (.out(P_out));
  Button C3 (.out(C3_out));
  Button C2 (.out(C2_out));
  Button C1 (.out(C1_out));
  detector detector_1 (.boton(N_out), .clk(ck), .reset(reset), .pulso(nuevoN));
  detector detector_2 (.boton(A_out), .clk(ck), .reset(reset), .pulso(nuevoA));
  detector detector_3 (.boton(P_out), .clk(ck), .reset(reset), .pulso(nuevoP));
  detector detector_4 (.boton(C3_out), .clk(ck), .reset(reset), .pulso(pC3));
  detector detector_5 (.boton(C2_out), .clk(ck), .reset(reset), .pulso(pC2));
  detector detector_6 (.boton(C1_out), .clk(ck), .reset(reset), .pulso(pC1));
  turnero Fila_N (
    .reset(reset), .ingreso(nuevoN), .clk(ck), .llamar(sigN), .E(dadosN), .llena(llenaN), .hay(hayN),
    .S(atendidosN));
  turnero Fila_A (
    .reset(reset), .ingreso(nuevoA), .clk(ck), .llamar(sigA), .E(dadosA), .llena(llenaA), .hay(hayA),
    .S(atendidosA));
  turnero Fila_P (
    .reset(reset), .ingreso(nuevoP), .clk(ck), .llamar(sigP), .E(dadosP), .llena(llenaP), .hay(hayP),
    .S(atendidosP));
  or or_1 (desocupado, pC1, pC2, pC3);
  not not_1 (no_hayP, hayP);
  not not_2 (no_hayA, hayA);
  and and_1 (sigP, desocupado, hayP);
  and and_2 (sigA, desocupado, no_hayP, hayA);
  and and_3 (ni_P_ni_A, no_hayP, no_hayA);
  and and_4 (sigN, desocupado, ni_P_ni_A, hayN);
  or or_2 (alguien_espera, hayP, hayA, hayN);
  and and_5 (llamar_ya, desocupado, alguien_espera);
  Register #(.width(4)) register_1 (.D(S_sig), .en(llamar_ya), .clk(ck), .Q(register_1_q), .clr(reset));
  Register #(.width(1)) register_2 (.D(sigP), .en(llamar_ya), .clk(ck), .Q(register_2_q), .clr(reset));
  Register #(.width(1)) register_3 (.D(sigA), .en(llamar_ya), .clk(ck), .Q(register_3_q), .clr(reset));
  Register #(.width(1)) register_4 (.D(sigN), .en(llamar_ya), .clk(ck), .Q(register_4_q), .clr(reset));
  Register #(.width(4)) register_5 (.D(cub_sig), .en(llamar_ya), .clk(ck), .Q(register_5_q), .clr(reset));
  Multiplexer #(.width(4)) multiplexer_1 (.in0(atendidosN), .in1(atendidosA), .out(S_AoN), .sel(hayA));
  Multiplexer #(.width(4)) multiplexer_2 (.in0(S_AoN), .in1(atendidosP), .out(S_sig), .sel(hayP));
  Multiplexer #(.width(4)) multiplexer_3 (.in0(4'b0001), .in1(4'b0010), .out(cub_1o2), .sel(pC2));
  Multiplexer #(.width(4)) multiplexer_4 (.in0(cub_1o2), .in1(4'b0011), .out(cub_sig), .sel(pC3));
  LED Fila_P_2 (.in(register_2_q));
  LED Fila_A_2 (.in(register_3_q));
  LED Fila_N_2 (.in(register_4_q));
  Hex_Digit_Display hex_digit_display_1 (.value(register_5_q));  // open: dp
  a_decimal a_decimal_1 (.n(register_1_q), .decenas(a_decimal_1_decenas), .unidades(a_decimal_1_unidades));
  Hex_Digit_Display hex_digit_display_2 (.value(a_decimal_1_decenas));  // open: dp
  Hex_Digit_Display hex_digit_display_3 (.value(a_decimal_1_unidades));  // open: dp
  and and_6 (and_6_out, nuevoP, no_llenaP);
  not not_3 (no_llenaP, llenaP);
  and and_7 (and_7_out, nuevoA, no_llenaA);
  not not_4 (no_llenaA, llenaA);
  and and_8 (and_8_out, nuevoN, no_llenaN);
  not not_5 (no_llenaN, llenaN);
  Register #(.width(4)) register_6 (.D(dadosP), .en(and_6_out), .clk(ck), .Q(register_6_q), .clr(reset));
  Register #(.width(4)) register_7 (.D(dadosA), .en(and_7_out), .clk(ck), .Q(register_7_q), .clr(reset));
  Register #(.width(4)) register_8 (.D(dadosN), .en(and_8_out), .clk(ck), .Q(register_8_q), .clr(reset));
  a_decimal a_decimal_2 (.n(register_6_q), .decenas(a_decimal_2_decenas), .unidades(a_decimal_2_unidades));
  a_decimal a_decimal_3 (.n(register_7_q), .decenas(a_decimal_3_decenas), .unidades(a_decimal_3_unidades));
  a_decimal a_decimal_4 (.n(register_8_q), .decenas(a_decimal_4_decenas), .unidades(a_decimal_4_unidades));
  Hex_Digit_Display hex_digit_display_4 (.value(a_decimal_2_decenas));  // open: dp
  Hex_Digit_Display hex_digit_display_5 (.value(a_decimal_3_decenas));  // open: dp
  Hex_Digit_Display hex_digit_display_6 (.value(a_decimal_4_decenas));  // open: dp
  Hex_Digit_Display hex_digit_display_7 (.value(a_decimal_2_unidades));  // open: dp
  Hex_Digit_Display hex_digit_display_8 (.value(a_decimal_3_unidades));  // open: dp
  Hex_Digit_Display hex_digit_display_9 (.value(a_decimal_4_unidades));  // open: dp
  LED Fila_llena (.in(llenaP));
  LED Fila_llena_2 (.in(llenaA));
  LED Fila_llena_3 (.in(llenaN));

  // Other names for the same wires on the sheet: clr = reset

  // Notes on the sheet:
  //   Activa el reloj con Ctrl+K y usa los botones
  //   Prioridad: P > A > N
  //   Cubiculo
  //   Pantalla de llamado
  //   Turno llamado
  //   Turno asignado al ingresar
  //   Fila P
  //   Fila A
  //   Fila N
endmodule

module detector (
  input  boton,
  input  clk,
  input  reset,
  output pulso
);

  wire antes, no_antes;

  D_Flip_Flop d_ff_1 (.D(boton), .clk(clk), .Q(antes), .reset(reset));  // open: Qn, preset
  not not_1 (no_antes, antes);
  and and_1 (pulso, boton, no_antes);

  // Notes on the sheet:
  //   pulso = boton AND NOT(boton en el ciclo anterior)
endmodule

module a_decimal (
  input  [3:0] n,
  output [3:0] decenas,
  output [3:0] unidades
);

  wire mayor9;
  wire [3:0] n_menos10;

  Comparator #(.width(4), .mode("unsigned")) comparator_1 (.a(n), .b(4'b1001), .gt(mayor9));  // open: eq, lt
  Subtractor #(.width(4)) subtractor_1 (.a(n), .b(4'b1010), .out(n_menos10));  // open: bin, bout
  Multiplexer #(.width(4)) multiplexer_1 (.in0(n), .in1(n_menos10), .out(unidades), .sel(mayor9));
  Multiplexer #(.width(4)) multiplexer_2 (.in0(4'b0000), .in1(4'b0001), .out(decenas), .sel(mayor9));

  // Other names for the same wires on the sheet: dec[3:0] = decenas; uni[3:0] = unidades

  // Notes on the sheet:
  //   Convierte 0-15 a dos digitos decimales
endmodule

module turnero (
  input  reset,
  input  ingreso,
  input  clk,
  input  llamar,
  output [3:0] E,
  output llena,
  output hay,
  output [3:0] S
);

  wire and_1_out, comparator_1_eq, counter_1_carry, not_2_out;
  wire [3:0] adder_1_out, undriven;

  Counter #(.max('hf), .width(4)) counter_1 (
    .clr(reset), .load(1'b0), .up(1'b1), .count(and_1_out), .clk(clk), .D(undriven), .carry(counter_1_carry),
    .Q(E));
  and and_1 (and_1_out, not_2_out, ingreso);
  Counter #(.max('hf), .width(4)) counter_2 (
    .clr(reset), .load(1'b0), .up(1'b1), .count(llamar), .clk(clk), .Q(S));  // open: D, carry
  Adder #(.width(4)) adder_1 (.a(E), .b(4'b0001), .out(adder_1_out));  // open: cin, cout
  not not_1 (hay, comparator_1_eq);
  Comparator #(.width(4)) comparator_1 (.a(E), .b(S), .eq(comparator_1_eq));  // open: gt, lt
  not not_2 (not_2_out, llena);
  Comparator #(.width(4)) comparator_2 (.a(adder_1_out), .b(S), .eq(llena));  // open: gt, lt
endmodule
