// Logisim project parqueader.circ as structural Verilog: 1 circuit, main circuit main
module main (
);

  wire and_1_out, and_2_out, comparator_1_gt, comparator_2_gt, ENTRA_out, not_1_out, or_1_out, RESET_out,
       SALE_out;
  wire [3:0] bit_extender_1_out, bit_extender_2_out;
  wire [6:0] adder_1_out, CARROS_q, divider_1_out, divider_1_rem, multiplexer_1_out, multiplexer_2_out,
       multiplexer_3_out;

  Button ENTRA (.out(ENTRA_out));
  Button SALE (.out(SALE_out));
  Button RESET (.out(RESET_out));
  and and_1 (and_1_out, ENTRA_out, comparator_1_gt);
  and and_2 (and_2_out, SALE_out, comparator_2_gt);
  or or_1 (or_1_out, and_1_out, and_2_out);
  Multiplexer #(.width(7), .enable("false")) multiplexer_1 (
    .in0(7'b0000001), .in1({7{1'b1}}), .out(multiplexer_1_out), .sel(SALE_out));
  Adder #(.width(7)) adder_1 (.a(CARROS_q), .b(multiplexer_1_out), .out(adder_1_out));  // open: cin, cout
  Register #(.width(7), .trigger("falling")) CARROS (
    .D(adder_1_out), .Q(CARROS_q), .clk(or_1_out), .clr(RESET_out));  // open: en
  Comparator #(.width(7), .mode("unsigned")) comparator_1 (
    .a(7'b0010100), .b(CARROS_q), .gt(comparator_1_gt));  // open: eq, lt
  Comparator #(.width(7), .mode("unsigned")) comparator_2 (
    .a(CARROS_q), .b({7{1'b0}}), .gt(comparator_2_gt));  // open: eq, lt
  Divider #(.width(7), .mode("unsigned")) divider_1 (
    .a(CARROS_q), .b(7'b0001010), .out(divider_1_out), .rem(divider_1_rem));  // open: upper
  LED HAY_CUPO (.in(comparator_1_gt));
  not not_1 (not_1_out, comparator_1_gt);
  Bit_Extender #(.in_width(7), .out_width(4), .\type ("zero")) bit_extender_1 (
    .in(divider_1_out), .out(bit_extender_1_out));
  Bit_Extender #(.in_width(7), .out_width(4), .\type ("zero")) bit_extender_2 (
    .in(divider_1_rem), .out(bit_extender_2_out));
  LED LLENO (.in(not_1_out));
  Multiplexer #(.select(4), .width(7), .enable("false")) multiplexer_2 (
    .in0(7'b0111111), .in1(7'b0000110), .in2(7'b1011011), .in3(7'b1001111), .in4(7'b1100110),
    .in5(7'b1101101), .in6(7'b1111101), .in7(7'b0000111), .in8({7{1'b1}}), .in9(7'b1101111),
    .out(multiplexer_2_out), .sel(bit_extender_1_out));  // open: in10, in11, in12, in13, in14, in15
  _7_Segment_Display #(.decimalPoint("false")) DECENAS (
    .g(multiplexer_2_out[6]), .f(multiplexer_2_out[5]), .a(multiplexer_2_out[0]), .b(multiplexer_2_out[1]),
    .e(multiplexer_2_out[4]), .d(multiplexer_2_out[3]), .c(multiplexer_2_out[2]));
  Multiplexer #(.select(4), .width(7), .enable("false")) multiplexer_3 (
    .in0(7'b0111111), .in1(7'b0000110), .in2(7'b1011011), .in3(7'b1001111), .in4(7'b1100110),
    .in5(7'b1101101), .in6(7'b1111101), .in7(7'b0000111), .in8({7{1'b1}}), .in9(7'b1101111),
    .out(multiplexer_3_out), .sel(bit_extender_2_out));  // open: in10, in11, in12, in13, in14, in15
  _7_Segment_Display #(.decimalPoint("false")) UNIDADES (
    .g(multiplexer_3_out[6]), .f(multiplexer_3_out[5]), .a(multiplexer_3_out[0]), .b(multiplexer_3_out[1]),
    .e(multiplexer_3_out[4]), .d(multiplexer_3_out[3]), .c(multiplexer_3_out[2]));
endmodule
